# Fritzing sketch Education Shield (saved by Fritzing 0.9.3b)
circuit board: 5.36311cm x 6.88566cm
breadboards: 1

parts:
  R1 = Resistor [tolerance=±5% resistance=220 package=THT]
  LED-D3 = LED - 5mm [color="Red (633nm)" package="5 mm [THT]"]
  R2 = Resistor [tolerance=±5% resistance=220 package=THT]
  Button-D8 = Pushbutton [package=THT]
  LED2 = RGB LED (com. cathode, rgb) [package="5 mm [THT]"]
  R3 = Resistor [tolerance=±5% resistance=220 package=THT]
  R4 = Resistor [tolerance=±5% resistance=220 package=THT]
  R5 = Resistor [tolerance=±5% resistance=220 package=THT]
  R6 = Resistor [tolerance=±5% resistance=220 package=THT]
  Switch-D7 = Toggle Switch [package=THT]
  Light_Detector-A1 = PHOTOCELL [package=photocell-kit]
  J2 = female pin header, 8 pins [form="♀ (female)"]
  J4 = female pin header, 6 pins [form="♀ (female)"]
  J3 = female pin header, 8 pins [form="♀ (female)"]
  J1 = female pin header, 10 pins [form="♀ (female)"]
  UART/BT/WIFI = female pin header, 4 pins [form="♀ (female)"]
  R7 = Resistor [tolerance=±5% resistance=220 package=THT]
  R8 = Resistor [tolerance=±5% resistance=220 package=THT]
  Hall_Sensor-D4 = female pin header, 3 pins [form="♀ (female)"]
  J6 = female pin header, 1 pin [form="♀ (female)"]
  Vibration-D5 = female pin header, 3 pins [form="♀ (female)"]
  TEMP-A2 = TMP36 Temperature Sensor [package="TO92 [THT]"]
  Piezo-D6 = female pin header, 1 pin [form="♀ (female)"]
  J8 = female pin header, 1 pin [form="♀ (female)"]
  J9 = female pin header, 4 pins [form="♀ (female)"]
  Potentiometer-A0 = female pin header, 1 pin [form="♀ (female)"]
  J11 = female pin header, 1 pin [form="♀ (female)"]
  J12 = female pin header, 1 pin [form="♀ (female)"]

nets:
  N1: R1.Pin_0, J2.pin5
  N2: R1.Pin_1, LED-D3.anode
  N3: LED-D3.cathode, LED2.common_cathode, R5.Pin_1, R6.Pin_0, Switch-D7.L2, J3.pin7, UART/BT/WIFI.pin3, R7.Pin_1, Hall_Sensor-D4.pin2, J6.pin1, Vibration-D5.pin2, Vibration-D5.pin3, TEMP-A2.GND, J9.pin2, J11.pin1
  N4: R2.Pin_0, LED2.red_anode
  N5: R2.Pin_1, J1.pin7
  N6: Button-D8.leg0, Switch-D7.L1, Light_Detector-A1.P$1, J3.pin5, UART/BT/WIFI.pin4, R8.Pin_0, Hall_Sensor-D4.pin1, TEMP-A2.+Vs, J9.pin1, Potentiometer-A0.pin1
  N7: Button-D8.leg1, R5.Pin_0, J1.pin10
  N8: LED2.green_anode, R3.Pin_0
  N9: LED2.blue_anode, R4.Pin_0
  N10: R3.Pin_1, J1.pin8
  N11: R4.Pin_1, J1.pin9
  N12: R6.Pin_1, Piezo-D6.pin1
  N13: Switch-D7.COM, J2.pin1
  N14: Light_Detector-A1.P$2, J4.pin2, R7.Pin_0
  N15: J2.pin2, J8.pin1
  N16: J2.pin3, Vibration-D5.pin1
  N17: J2.pin4, R8.Pin_1, Hall_Sensor-D4.pin3
  N18: J2.pin6, UART/BT/WIFI.pin2
  N19: J4.pin1, J12.pin1
  N20: J4.pin3, TEMP-A2.Vout
  N21: J4.pin5, J9.pin4
  N22: J4.pin6, J9.pin3
  N23: J1.pin6, UART/BT/WIFI.pin1

notes:
  Education Shield
  ON      OFF
  R-D11
  B-D10
  G-D9
  TX-D2
  RX-D12
  5V
  GND
  +
  HIGH
  LOW
  A5
  A4
